# Fritzing sketch arcdryier (saved by Fritzing 0.9.6b)

parts:
  F1 = Fan - 4 wire [package=THT]
  J2 = Power Jack [package=power_jack_smd]
  U1 = DC 5V TO ± 12V Mini DC converter [package=THT]
  R1 = Rotary Potentiometer (Small) [maximum_resistance=100kΩ package=THT]
  R2 = Rotary Potentiometer (Small) [maximum_resistance=100kΩ package=THT]
  Mod2 = ESP32-TTGO-T-DISPLAY

nets:
  GND: F1.GND, J2.GND
  N1: F1.Power, J2.PWR
  N2: U1.GND, Mod2.G-11
  N3: U1.-12V, Mod2.5V
  N4: R1.wiper, Mod2.36
  N5: R2.wiper, Mod2.39

custom parts:
  Fan - 4 wire: Fan, 4 wire with tach.
  DC 5V TO ± 12V Mini DC converter: DC 5V TO ± 12V Mini DC converter from ebay (search for "DC 5V TO ± 12V Mini DC converter"). Supplies ± 12V at up to 30MA output for op amps or rs232 drivers from a 3 to 5V input (so a battery or 3.3 or 5V power rail) on a micro).
  ESP32-TTGO-T-DISPLAY: LILYGO TTGO T-Display GD32VF103CBT6 Main Chip ST7789 1.14 Inch IPS 240x135 Resolution Minimalist Development Board.
